// Digital circuit day2.dig as structural Verilog
module day2 (
  input  clk,
  output [63:0] ram_0
);

  wire and_1_out, comparator_1_eq, intcode_1_p5;
  wire [15:0] intcode_1_p4;
  wire [63:0] intcode_1_p3;

  // intcode intcode_1: pin names not known; wires that end beside it: clk, {64{1'b0}}, intcode_1_p3, intcode_1_p4, intcode_1_p5
  Comparator #(.Bits(16)) comparator_1 (.a(intcode_1_p4), .b({16{1'b0}}), .eq(comparator_1_eq));  // open: gt, lt
  and and_1 (and_1_out, comparator_1_eq, intcode_1_p5);
  Register #(.Bits(64)) register_1 (.D(intcode_1_p3), .C(clk), .en(and_1_out), .Q(ram_0));

  // Other names for the same wires on the sheet: C = clk
endmodule
