// Digital circuit intcode.dig as structural Verilog
module intcode (
  input  clock,
  output [63:0] write_val,
  output [15:0] rw_addr,
  output str,
  output [15:0] pc,
  output [63:0] last_in,
  output [63:0] last_out,
  output [63:0] X,
  output [63:0] Y,
  output [63:0] r,
  output [63:0] instr,
  output [7:0] n_out
);

  wire and_1_out, and_2_out, and_3_out, and_4_out, and_5_out, and_6_out, and_7_out, and_8_out, and_9_out,
       and_10_out, comparator_1_eq, comparator_2_eq, comparator_3_eq, decoder_1_out_0, decoder_1_out_1,
       decoder_1_out_2, decoder_1_out_3, decoder_2_out_1, decoder_2_out_2, decoder_2_out_3, decoder_2_out_4,
       decoder_2_out_5, decoder_2_out_6, nor_1_out, nor_2_out, or_1_out, or_2_out, or_4_out, run_q,
       sub_1_c_o, sub_2_c_o;
  wire [1:0] phase_out;
  wire [3:0] multiplexer_5_out;
  wire [7:0] counter_1_out;
  wire [15:0] add_1_s, add_2_s, multiplexer_1_out, multiplexer_6_out;
  wire [31:0] cycles_out, icount_out;
  wire [63:0] at_0_q, input_d, mul_mul, multiplexer_3_out, multiplexer_4_out, plus_s, ram_d1, sub_1_s,
       sub_2_s;
  wire [63:16] multiplexer_6_out_2, ram_d2;

  // Probe on at_0_q
  Register #(.Bits(64)) at_0 (.D(write_val), .C(and_2_out), .en(and_1_out), .Q(at_0_q));
  and and_1 (and_1_out, comparator_1_eq, str);
  LED running (.in(run_q));
  and and_2 (and_2_out, run_q, clock);
  Comparator #(.Bits(16)) comparator_1 (.a({16{1'b0}}), .b(rw_addr), .eq(comparator_1_eq));  // open: gt, lt
  Counter #(.Bits(32)) cycles (.en(run_q), .C(and_2_out), .clr(1'b0), .out(cycles_out));  // open: ovf
  T_FF #(.Default(1)) run (.T(and_5_out), .C(and_2_out), .Q(run_q));  // open: nQ
  // Probe on cycles_out
  Break break_1 (.brk(str));
  Break break_2 (.brk(and_5_out));
  Add #(.Bits(16)) add_1 (.a(pc), .b({{14{1'b0}}, phase_out}), .c_i(1'b1), .s(add_1_s));  // open: c_o
  Add #(.Bits(16)) add_2 (.a({{14{1'b0}}, phase_out}), .b(pc), .c_i(1'b0), .s(add_2_s));  // open: c_o
  RAMDualAccess #(.AddrBits(16), .Bits(64), .isProgramMemory("true")) ram (
    .str(str), .C(and_2_out), .ld(1'b1), .A1(rw_addr), .Din1(write_val), .A2(add_2_s), .D1(ram_d1),
    .D2({ram_d2, rw_addr}));
  Multiplexer #(.Bits(16)) multiplexer_1 (
    .sel(or_1_out), .in_0(add_1_s), .in_1(multiplexer_6_out), .out(multiplexer_1_out));
  Register #(.Bits(16)) u_pc (.D(multiplexer_1_out), .C(and_2_out), .en(or_2_out), .Q(pc));
  or or_1 (or_1_out, and_4_out, and_3_out);
  or or_2 (or_2_out, and_10_out, and_7_out, str);
  and and_3 (and_3_out, comparator_3_eq, decoder_2_out_5);
  and and_4 (and_4_out, ~comparator_3_eq, decoder_2_out_6);  // And
  Counter #(.Bits(32)) icount (.en(decoder_1_out_0), .C(and_2_out), .clr(1'b0), .out(icount_out));  // open: ovf
  Counter #(.Bits(2)) phase (.en(1'b1), .C(and_2_out), .clr(or_2_out), .out(phase_out));  // open: ovf
  // Probe on icount_out
  Register #(.Bits(64)) register_1 (.D({ram_d2, rw_addr}), .C(and_2_out), .en(decoder_1_out_0), .Q(instr));
  // Probe on phase_out
  Decoder #(.Selector_Bits(2)) decoder_1 (
    .sel(phase_out), .out_0(decoder_1_out_0), .out_1(decoder_1_out_1), .out_2(decoder_1_out_2),
    .out_3(decoder_1_out_3));
  Break break_3 (.brk(decoder_2_out_5));
  or or_3 (str, and_9_out, decoder_1_out_3);
  and and_5 (and_5_out, decoder_1_out_1, nor_2_out);
  Multiplexer #(.Bits(64)) multiplexer_2 (.sel(and_9_out), .in_0(r), .in_1(input_d), .out(write_val));
  Sub #(.Bits(64)) sub_1 (.a(instr), .b(64'h3e8), .c_i(1'b0), .s(sub_1_s), .c_o(sub_1_c_o));
  and and_6 (and_6_out, ~sub_1_c_o, decoder_1_out_2);  // And
  and and_7 (and_7_out, or_4_out, decoder_1_out_2);
  Multiplexer #(.Bits(64)) multiplexer_3 (.sel(sub_1_c_o), .in_0(sub_1_s), .in_1(instr), .out(multiplexer_3_out));
  Counter #(.Bits(8)) counter_1 (.en(and_9_out), .C(and_2_out), .clr(1'b0), .out(counter_1_out));  // open: ovf
  or or_4 (or_4_out, decoder_2_out_5, decoder_2_out_6);
  ROM #(.AddrBits(8), .Bits(64)) \input  (.A(counter_1_out), .sel(1'b1), .D(input_d));
  Sub #(.Bits(64)) sub_2 (.a(multiplexer_3_out), .b(64'h64), .c_i(1'b0), .s(sub_2_s), .c_o(sub_2_c_o));
  and and_8 (and_8_out, ~sub_2_c_o, decoder_1_out_1);  // And
  Multiplexer #(.Bits(64)) multiplexer_4 (
    .sel(sub_2_c_o), .in_0(sub_2_s), .in_1(multiplexer_3_out), .out(multiplexer_4_out));
  Register #(.Bits(64)) register_2 (.D(input_d), .C(and_2_out), .en(and_9_out), .Q(last_in));
  Register #(.Bits(64)) register_3 (
    .D({multiplexer_6_out_2, multiplexer_6_out}), .C(and_2_out), .en(and_10_out), .Q(last_out));
  RAMDualPort #(.AddrBits(8), .Bits(64)) \output  (
    .A(n_out), .Din({multiplexer_6_out_2, multiplexer_6_out}), .str(and_10_out), .C(and_2_out), .ld(1'b1));  // open: D
  Comparator #(.Bits(64)) comparator_2 (.a(multiplexer_4_out), .b(64'h63), .eq(comparator_2_eq));  // open: gt, lt
  Counter #(.Bits(8)) counter_2 (.en(and_10_out), .C(and_2_out), .clr(1'b0), .out(n_out));  // open: ovf
  nor nor_1 (nor_1_out, and_6_out, and_8_out);
  Multiplexer #(.Bits(4)) multiplexer_5 (
    .sel(comparator_2_eq), .in_0(multiplexer_4_out[3:0]), .in_1(4'b1111), .out(multiplexer_5_out));
  Multiplexer #(.Bits(64)) multiplexer_6 (
    .sel(nor_1_out), .in_0({ram_d2, rw_addr}), .in_1(ram_d1), .out({multiplexer_6_out_2, multiplexer_6_out}));
  and and_9 (and_9_out, decoder_2_out_3, decoder_1_out_1);
  and and_10 (and_10_out, decoder_2_out_4, decoder_1_out_1);
  Decoder #(.Selector_Bits(4)) decoder_2 (
    .sel(multiplexer_5_out), .out_1(decoder_2_out_1), .out_2(decoder_2_out_2), .out_3(decoder_2_out_3),
    .out_4(decoder_2_out_4), .out_5(decoder_2_out_5), .out_6(decoder_2_out_6));  // open: out_0, out_7, out_8, out_9, out_10, out_11, out_12, out_13, out_14, out_15
  Register #(.Bits(64)) register_4 (
    .D({multiplexer_6_out_2, multiplexer_6_out}), .C(and_2_out), .en(decoder_1_out_1), .Q(X));
  Add #(.Bits(64)) plus (.a(X), .b(Y), .c_i(1'b0), .s(plus_s));  // open: c_o
  Comparator #(.Signed("true"), .Bits(64)) comparator_3 (.a({64{1'b0}}), .b(X), .eq(comparator_3_eq));  // open: gt, lt
  nor nor_2 (nor_2_out, decoder_2_out_1, decoder_2_out_2, decoder_2_out_3, decoder_2_out_4, decoder_2_out_5, decoder_2_out_6);
  Register #(.Bits(64)) register_5 (
    .D({multiplexer_6_out_2, multiplexer_6_out}), .C(and_2_out), .en(decoder_1_out_2), .Q(Y));
  Mul #(.Bits(32), .Signed("true")) mul (.a(Y[31:0]), .b(X[31:0]), .mul(mul_mul));
  Multiplexer #(.Bits(64)) multiplexer_7 (.sel(decoder_2_out_2), .in_0(plus_s), .in_1(mul_mul), .out(r));

  // Notes on the sheet:
  //   clock: Hz: 100
  //   Instruction decoding
  //   contents of input (hex, n*v repeats v):
  //   1
  //   Internal registers
  //   ALU
endmodule
